// Digital circuit nna1.dig as structural Verilog
module nna1 (
  input  clk
);

  wire and_1_out, and_2_out, and_3_out, and_4_out, and_5_out, clock, decoder_1_out_0, decoder_2_out_0,
       decoder_2_out_1, decoder_2_out_2, decoder_3_out_0, decoder_3_out_1, decoder_3_out_2, decoder_3_out_3,
       not_1_out, not_2_out, not_3_out, oflag_q, or_1_out, or_3_out, switchdt_1_p3;
  wire [0:0] or_2_out;
  wire [3:0] multiplexer_1_out, multiplexer_2_out, r0_q, r1_q, r2_q, r3_q;
  wire [6:0] add_1_s, PC_q;
  wire [7:0] main_mem_d;

  Add #(.Bits(7)) add_1 (.a(PC_q), .b(7'b0000001), .c_i(1'b0), .s(add_1_s));  // open: c_o
  // SwitchDT switchdt_1: pin names not known; wires that end beside it: 1'b1, 1'b0, switchdt_1_p3
  Register #(.Bits(7), .isProgramCounter("true")) PC (.D(add_1_s), .C(clock), .en(1'b1), .Q(PC_q));
  // SwitchDT switchdt_2: pin names not known; wires that end beside it: clk, switchdt_1_p3, clock
  EEPROM #(.AddrBits(7), .isProgramMemory("true"), .Bits(8)) main_mem (
    .A(PC_q), .CS(1'b1), .WE(1'b0), .OE(1'b1), .D(main_mem_d));
  Decoder #(.Selector_Bits(4)) decoder_1 (
    .sel(main_mem_d[7:4]), .out_0(decoder_1_out_0));  // open: out_1, out_2, out_3, out_4, out_5, out_6, out_7, out_8, out_9, out_10, out_11, out_12, out_13, out_14, out_15
  Decoder #(.Selector_Bits(2)) decoder_2 (
    .sel(main_mem_d[3:2]), .out_0(decoder_2_out_0), .out_1(decoder_2_out_1), .out_2(decoder_2_out_2));  // open: out_3
  not not_1 (not_1_out, main_mem_d[0]);
  and and_1 (and_1_out, decoder_1_out_0, not_1_out, main_mem_d[1], decoder_2_out_0);
  and and_2 (and_2_out, decoder_2_out_1, decoder_1_out_0);
  and and_3 (and_3_out, decoder_1_out_0, decoder_2_out_2);
  and and_4 (and_4_out, decoder_1_out_0, main_mem_d[0], main_mem_d[1], decoder_2_out_0);
  or or_1 (or_1_out, and_2_out, not_2_out);
  not not_2 (not_2_out, and_3_out);
  or or_2 (or_2_out[0], and_2_out, and_3_out);
  LED flf (.in(and_1_out));
  LED cfl (.in(and_4_out));
  LED shl (.in(and_2_out));
  LED shr (.in(and_3_out));
  Multiplexer #(.Bits(4)) multiplexer_1 (
    .sel(or_1_out), .in_0({1'b0, multiplexer_2_out[3:1]}), .in_1({multiplexer_2_out[2:0], 1'b0}),
    .out(multiplexer_1_out));
  and and_5 (and_5_out, not_3_out, and_1_out);
  or or_3 (or_3_out, and_1_out, and_4_out);
  Decoder #(.Selector_Bits(3)) decoder_3 (
    .sel({main_mem_d[1:0], or_2_out[0]}), .out_0(decoder_3_out_0), .out_1(decoder_3_out_1),
    .out_2(decoder_3_out_2), .out_3(decoder_3_out_3));  // open: out_4, out_5, out_6, out_7
  not not_3 (not_3_out, oflag_q);
  Register oflag (.D(and_5_out), .C(clock), .en(or_3_out), .Q(oflag_q));
  LED oflag_2 (.in(oflag_q));
  Register #(.Bits(4)) r0 (.D(multiplexer_1_out), .C(clock), .en(decoder_3_out_0), .Q(r0_q));
  Register #(.Bits(4)) r1 (.D(multiplexer_1_out), .C(clock), .en(decoder_3_out_1), .Q(r1_q));
  Register #(.Bits(4)) r2 (.D(multiplexer_1_out), .C(clock), .en(decoder_3_out_2), .Q(r2_q));
  Register #(.Bits(4)) r3 (.D(multiplexer_1_out), .C(clock), .en(decoder_3_out_3), .Q(r3_q));
  Multiplexer #(.Bits(4), .Selector_Bits(2)) multiplexer_2 (
    .sel(main_mem_d[1:0]), .in_0(r0_q), .in_1(r1_q), .in_2(r2_q), .in_3(r3_q), .out(multiplexer_2_out));

  // Notes on the sheet:
  //   contents of main_mem (hex, n*v repeats v):
  //   0,2,3,2,2
  //   op decoder
  //   opcode
  //   opcode = 0
  //   arg0
  //   arg1
  //   arg0 = 0
  //   shl
  //   shr
  //   sel reg shifted left
  //   sel reg shifted right
  //   registers
  //   out reg select
  //   in reg select
  //   enable
  //   in value
  //   sel reg out value
  //   out value
endmodule
