// Digital circuit nna8v0.dig as structural Verilog
module nna8v0 (
  input  clk
);

  wire add, add_1_c_o, add_2_c_o, \and , and_1_out, and_2_out, and_3_out, and_4_out, and_5_out, and_9_out,
       and_10_out, and_11_out, and_12_out, and_13_out, and_14_out, and_15_out, and_24_out, and_25_out,
       and_26_out, and_27_out, and_28_out, and_29_out, bra, brk, clf, comparator_1_eq, comparator_1_lt, dec,
       decoder_1_out_0, decoder_1_out_1, decoder_1_out_2, decoder_1_out_3, decoder_2_out_0, decoder_3_out_0,
       decoder_3_out_1, decoder_3_out_2, decoder_3_out_3, eq, firstcycle, flf, gt, inc, jmp, lih, lil, mov,
       mrd, mul, mwr, nop, \not , not_1_out, not_2_out, not_3_out, not_4_out, not_5_out, not_6_out,
       not_7_out, not_8_out, not_9_out, not_11_out, not_12_out, not_13_out, not_14_out, not_15_out,
       not_16_out, not_17_out, not_18_out, not_19_out, not_20_out, not_21_out, oflag_out, \or , or_1_out,
       or_2_out, or_3_out, or_4_out, or_5_out, or_7_out, or_8_out, pc_write, rol, sub_1_c_o, \xor ;
  wire [1:0] and_6_out;
  wire [3:0] arg, curop_q;
  wire [7:0] add_1_s, add_2_s, addrbus, and_23_out, barrelshifter_1_out, barrelshifter_2_out, mbus,
       not_10_out, or_6_out, pc, pc_next, r1_q, r2_q, r3_q, regin, regout_arg0, regout_arg1, regout_r0,
       sub_1_s, xor_1_out;
  wire [15:0] mul_1_mul;

  and and_1 (and_1_out, ~firstcycle, mwr);  // And
  CounterPreset #(.Bits(8), .isProgramCounter("true")) u_PC (
    .en(firstcycle), .C(clk), .dir(1'b0), .in(pc_next), .ld(pc_write), .clr(1'b0), .out(pc));  // open: ovf
  and and_2 (and_2_out, clk, and_1_out);
  or or_1 (or_1_out, mwr, mrd);
  or or_2 (or_2_out, bra, jmp);
  and and_3 (and_3_out, ~firstcycle, or_1_out);  // And
  and and_4 (and_4_out, ~firstcycle, mrd);  // And
  and and_5 (and_5_out, ~firstcycle, mwr);  // And
  or or_3 (or_3_out, brk, nop);
  or or_4 (or_4_out, lil, lih);
  not not_1 (not_1_out, jmp);
  TransGate #(.Bits(8)) transgate_1 (.A(firstcycle), .nA(not_2_out), .out1(pc), .out2(addrbus));
  not not_2 (not_2_out, firstcycle);
  T_FF t_ff_1 (.T(1'b1), .C(clk), .nQ(firstcycle));  // open: Q
  EEPROM #(.AddrBits(8), .isProgramMemory("true"), .Bits(8)) eeprom_1 (
    .A(addrbus), .CS(~clk), .WE(and_2_out), .OE(~and_1_out), .D(mbus));
  or or_5 (or_5_out, mwr, bra, gt, eq, flf, clf, jmp, or_3_out);
  and and_6 (and_6_out[1], arg[3], ~or_4_out);  // And
  and and_7 (and_6_out[0], arg[2], ~or_4_out);  // And
  and and_8 (pc_write, or_2_out, ~oflag_out);  // And
  TransGate #(.Bits(8)) transgate_2 (.A(jmp), .nA(not_1_out), .out1(regout_arg0), .out2(pc_next));
  TransGate #(.Bits(8)) transgate_3 (.A(bra), .nA(not_3_out), .out1({pc[7:4], arg}), .out2(pc_next));
  not not_3 (not_3_out, bra);
  LED led_1 (.in(firstcycle));
  TransGate #(.Bits(8)) transgate_4 (.A(and_3_out), .nA(not_4_out), .out1(regout_arg1), .out2(addrbus));
  not not_4 (not_4_out, and_3_out);
  TransGate #(.Bits(8)) transgate_5 (.A(and_4_out), .nA(not_5_out), .out1(mbus), .out2(regin));
  not not_5 (not_5_out, and_4_out);
  TransGate #(.Bits(8)) transgate_6 (.A(and_5_out), .nA(not_6_out), .out1(regout_arg0), .out2(mbus));
  not not_6 (not_6_out, and_5_out);
  and and_9 (and_9_out, ~or_5_out, ~firstcycle);  // And
  Decoder #(.Selector_Bits(2)) decoder_1 (
    .sel(and_6_out), .out_0(decoder_1_out_0), .out_1(decoder_1_out_1), .out_2(decoder_1_out_2),
    .out_3(decoder_1_out_3));
  and and_10 (and_10_out, and_9_out, decoder_1_out_0);
  and and_11 (and_11_out, and_9_out, decoder_1_out_1);
  and and_12 (and_12_out, and_9_out, decoder_1_out_2);
  and and_13 (and_13_out, and_9_out, decoder_1_out_3);
  Decoder #(.Selector_Bits(4)) decoder_2 (
    .sel(curop_q), .out_0(decoder_2_out_0), .out_1(lil), .out_2(lih), .out_3(mwr), .out_4(mrd), .out_5(mov),
    .out_6(bra), .out_7(rol), .out_8(eq), .out_9(gt), .out_10(add), .out_11(mul), .out_12(\and ),
    .out_13(\not ), .out_14(\or ), .out_15(\xor ));
  Register #(.Bits(8)) curop (.D(mbus), .C(clk), .en(firstcycle), .Q({curop_q, arg}));
  Decoder #(.Selector_Bits(2)) decoder_3 (
    .sel(arg[1:0]), .out_0(decoder_3_out_0), .out_1(decoder_3_out_1), .out_2(decoder_3_out_2),
    .out_3(decoder_3_out_3));
  and and_14 (and_14_out, ~arg[2], ~arg[3]);  // And
  and and_15 (and_15_out, arg[2], ~arg[3]);  // And
  LED led_2 (.in(arg[2]));
  LED led_3 (.in(arg[3]));
  LED led_4 (.in(arg[0]));
  LED led_5 (.in(arg[1]));
  Register #(.Bits(8)) r0 (.D(regin), .C(clk), .en(and_10_out), .Q(regout_r0));
  Register #(.Bits(8)) r1 (.D(regin), .C(clk), .en(and_11_out), .Q(r1_q));
  Register #(.Bits(8)) r2 (.D(regin), .C(clk), .en(and_12_out), .Q(r2_q));
  Register #(.Bits(8)) r3 (.D(regin), .C(clk), .en(and_13_out), .Q(r3_q));
  not not_7 (not_7_out, arg[2]);
  and and_16 (nop, and_14_out, decoder_3_out_0, decoder_2_out_0);
  and and_17 (brk, and_15_out, decoder_3_out_0, decoder_2_out_0);
  Break #(.Cycles(1000000)) u_brk (.brk(brk));
  and and_18 (jmp, decoder_3_out_1, decoder_2_out_0);
  and and_19 (inc, decoder_2_out_0, decoder_3_out_2);
  and and_20 (dec, decoder_2_out_0, decoder_3_out_3);
  and and_21 (flf, decoder_2_out_0, decoder_3_out_0, not_7_out, arg[3]);
  and and_22 (clf, decoder_2_out_0, decoder_3_out_0, arg[2], arg[3]);
  Multiplexer #(.Selector_Bits(2), .Bits(8)) multiplexer_1 (
    .sel(arg[3:2]), .in_0(regout_r0), .in_1(r1_q), .in_2(r2_q), .in_3(r3_q), .out(regout_arg0));
  Multiplexer #(.Selector_Bits(2), .Bits(8)) multiplexer_2 (
    .sel(arg[1:0]), .in_0(regout_r0), .in_1(r1_q), .in_2(r2_q), .in_3(r3_q), .out(regout_arg1));
  LED led_6 (.in(nop));
  LED led_7 (.in(brk));
  LED led_8 (.in(flf));
  LED led_9 (.in(clf));
  LED led_10 (.in(jmp));
  LED led_11 (.in(inc));
  LED led_12 (.in(dec));
  LED led_13 (.in(lil));
  LED led_14 (.in(lih));
  LED led_15 (.in(mwr));
  LED led_16 (.in(mrd));
  LED led_17 (.in(mov));
  LED led_18 (.in(bra));
  LED led_19 (.in(rol));
  LED led_20 (.in(eq));
  LED led_21 (.in(gt));
  LED led_22 (.in(add));
  LED led_23 (.in(mul));
  LED led_24 (.in(\and ));
  LED led_25 (.in(\not ));
  LED led_26 (.in(\or ));
  LED led_27 (.in(\xor ));
  not not_8 (not_8_out, oflag_out);
  not not_9 (not_9_out, mov);
  TransGate #(.Bits(8)) transgate_7 (.A(mov), .nA(not_9_out), .out1(regout_arg1), .out2(regin));
  Add #(.Bits(8)) add_1 (.a(regout_arg0), .b(8'h1), .c_i(oflag_out), .s(add_1_s), .c_o(add_1_c_o));
  Sub #(.Bits(8)) sub_1 (.a(regout_arg0), .b(8'h1), .c_i(oflag_out), .s(sub_1_s), .c_o(sub_1_c_o));
  assign and_23_out = regout_arg0 & regout_arg1;  // And and_23, 8 bits wide
  assign not_10_out = ~regout_arg1;  // Not not_10, 8 bits wide
  assign or_6_out = regout_arg0 | regout_arg1;  // Or or_6, 8 bits wide
  assign xor_1_out = regout_arg0 ^ regout_arg1;  // XOr xor_1, 8 bits wide
  TransGate #(.Bits(8)) transgate_8 (.A(lil), .nA(not_11_out), .out1({regout_r0[7:4], arg}), .out2(regin));
  not not_11 (not_11_out, lil);
  TransGate #(.Bits(8)) transgate_9 (.A(lih), .nA(not_12_out), .out1({arg, regout_r0[3:0]}), .out2(regin));
  not not_12 (not_12_out, lih);
  and and_24 (and_24_out, flf, not_8_out);
  TransGate #(.Bits(8)) transgate_10 (.A(inc), .nA(not_13_out), .out1(add_1_s), .out2(regin));
  and and_25 (and_25_out, add_1_c_o, inc);
  TransGate #(.Bits(8)) transgate_11 (.A(dec), .nA(not_14_out), .out1(sub_1_s), .out2(regin));
  and and_26 (and_26_out, sub_1_c_o, dec);
  TransGate #(.Bits(8)) transgate_12 (.A(\and ), .nA(not_15_out), .out1(and_23_out), .out2(regin));
  TransGate #(.Bits(8)) transgate_13 (.A(\not ), .nA(not_16_out), .out1(not_10_out), .out2(regin));
  TransGate #(.Bits(8)) transgate_14 (.A(\or ), .nA(not_17_out), .out1(or_6_out), .out2(regin));
  TransGate #(.Bits(8)) transgate_15 (.A(\xor ), .nA(not_18_out), .out1(xor_1_out), .out2(regin));
  not not_13 (not_13_out, inc);
  not not_14 (not_14_out, dec);
  not not_15 (not_15_out, \and );
  not not_16 (not_16_out, \not );
  not not_17 (not_17_out, \or );
  not not_18 (not_18_out, \xor );
  Comparator #(.Bits(8)) comparator_1 (
    .a(regout_arg0), .b(regout_arg1), .eq(comparator_1_eq), .lt(comparator_1_lt));  // open: gt
  Add #(.Bits(8)) add_2 (.a(regout_arg0), .b(regout_arg1), .c_i(oflag_out), .s(add_2_s), .c_o(add_2_c_o));
  Mul #(.Bits(8)) mul_1 (.a(regout_arg0), .b(regout_arg1), .mul(mul_1_mul));
  BarrelShifter #(.Bits(8), .barrelShifterMode("rotate")) barrelshifter_1 (
    .in(regout_arg0), .shift(regout_arg1[3:0]), .out(barrelshifter_1_out));
  TransGate #(.Bits(8)) transgate_16 (.A(add), .nA(not_19_out), .out1(add_2_s), .out2(regin));
  and and_27 (and_27_out, add_2_c_o, add);
  BarrelShifter #(.Bits(8), .barrelShifterMode("rotate")) barrelshifter_2 (
    .in(barrelshifter_1_out), .shift(regout_arg1[7:4]), .out(barrelshifter_2_out));
  and and_28 (and_28_out, eq, ~comparator_1_eq);  // And
  and and_29 (and_29_out, ~comparator_1_lt, gt);  // And
  not not_19 (not_19_out, add);
  not not_20 (not_20_out, mul);
  TransGate #(.Bits(8)) transgate_17 (.A(mul), .nA(not_20_out), .out1(mul_1_mul[7:0]), .out2(regin));
  not not_21 (not_21_out, rol);
  TransGate #(.Bits(8)) transgate_18 (.A(rol), .nA(not_21_out), .out1(barrelshifter_2_out), .out2(regin));
  or or_7 (or_7_out, and_24_out, and_25_out, and_26_out, and_28_out, and_29_out, and_27_out);
  or or_8 (or_8_out, flf, clf, eq, gt, dec, inc);
  Register oflag (.D(or_7_out), .C(clk), .en(or_8_out), .Q(oflag_out));
  LED oflag_2 (.in(oflag_out));

  // Other names for the same wires on the sheet: arg1[1:0] = arg[1:0]; arg0[1:0] = arg[3:2]; clock = clk

  // Notes on the sheet:
  //   clk: Hz: 2147483647
  //   main memory
  //   pc,clock
  //   mwr, mrd
  //   jmp bra
  //   registers
  //   select r0 on lil,lih ops
  //   contents of eeprom_1 (hex, n*v repeats v):
  //   22,58,4c,e,20,1e,33,3e,23,10,54,24,10,1,4,17*0,20,e,14*0,48,65
  //   ,6c,6c,6f,20,57,6f,72,6c,64,21,21,0,0,0,10,2f,58,4d,f0,83,6c,c
  //   ,3e,a,6,63,22,10,4c,47,f,33,5,157*0,48,65,6c,6c,6f,20,57,6f,72
  //   ,6c,64,21,21
  //   regin_addr
  //   op decoder
  //   write enable
  //   opcode = 0
  //   opcode
  //   arg1 = 0
  //   lil lih
  //   flf clf mov
  //   alu
  //   oflag
endmodule
